# Fritzing sketch GPIO Board (saved by Fritzing 1.0.5)
circuit board: 8.8984cm x 7.53128cm
breadboards: 1

parts:
  -_+_D = female pin header, 3 pins [form="♀ (female)"]
  S1_S2 = female pin header, 3 pins [form="♀ (female)"]
  PI_5 = Raspberry Pi 4B
  -_+_TxRx = female pin header, 4 pins [form="♀ (female)"]
  StepDown_LM2596 = RioRand LM2596
  V+_VCC_SDA_SCL_GND = female pin header, 5 pins [form="♀ (female)"]
  StepDown_LM2597 = RioRand LM2596
  V+_VCC_SDA_SCL_GND1 = female pin header, 5 pins [form="♀ (female)"]

nets:
  N1: -_+_D.pin1, PI_5.GPIO19
  N2: -_+_D.pin2, S1_S2.pin2, StepDown_LM2596.Pin_1, V+_VCC_SDA_SCL_GND.pin1, StepDown_LM2597.Pin_1
  N3: -_+_D.pin3, S1_S2.pin3, -_+_TxRx.pin1, StepDown_LM2596.Pin_2, StepDown_LM2596.Pin_4, StepDown_LM2597.Pin_2, StepDown_LM2597.Pin_4
  N4: S1_S2.pin1, PI_5.GPIO13
  N5: PI_5.5V, -_+_TxRx.pin2, StepDown_LM2596.Pin_3, V+_VCC_SDA_SCL_GND.pin2
  N6: PI_5.GPIO2, V+_VCC_SDA_SCL_GND.pin3, V+_VCC_SDA_SCL_GND1.pin3
  N7: PI_5.GPIO3, V+_VCC_SDA_SCL_GND.pin4, V+_VCC_SDA_SCL_GND1.pin4
  N8: PI_5.GPIO14, -_+_TxRx.pin3
  N9: PI_5.GND, V+_VCC_SDA_SCL_GND.pin5, V+_VCC_SDA_SCL_GND1.pin5
  N10: PI_5.GPIO15, -_+_TxRx.pin4
  N11: StepDown_LM2597.Pin_3, V+_VCC_SDA_SCL_GND1.pin1, V+_VCC_SDA_SCL_GND1.pin2
